// Logisim project minikit_logisim.circ as structural Verilog: 2 circuits, main circuit main
module main (
  input  x,
  input  A,
  input  F,
  input  y,
  input  z,
  input  B,
  input  in_7,
  input  in_8,
  input  in_9,
  input  x_2,
  input  y_2,
  input  in_12,
  input  z_2,
  input  in_14,
  input  in_15,
  input  in_16,
  input  in_17,
  input  in_18,
  input  in_19,
  input  in_20,
  input  in_21,
  input  in_22,
  input  in_23,
  input  in_24,
  input  in_25,
  input  in_26,
  input  in_27,
  input  in_28,
  input  in_29,
  input  in_30,
  input  in_31,
  input  in_32,
  input  in_33,
  input  in_34,
  input  in_35,
  input  in_36,
  input  in_37,
  input  in_38,
  input  in_39,
  input  in_40,
  input  in_41,
  input  in_42,
  input  a_2,
  input  Carry_in,
  input  b_2,
  input  c,
  input  d,
  input  a_3,
  input  b_3,
  input  Carry_in_2,
  input  D0,
  input  A0,
  input  A1,
  input  D1,
  input  D2,
  input  D3,
  input  [1:0] A_4,
  input  s1,
  input  s0,
  input  A0_2,
  input  A0_3,
  input  A1_2,
  input  A1_3,
  input  en1___1,
  input  Enable,
  input  en2a____0,
  input  en2b___0,
  input  [1:0] A_5,
  input  [1:0] A_6,
  input  en1___1_2,
  input  Enable_2,
  input  en2a____0_2,
  input  en2b___0_2,
  output cout,
  output s,
  output Q0,
  output Q0_2,
  output Q2,
  output Q1,
  output Q1_2,
  output Q3,
  output Q2_2,
  output Q3_2,
  output Q0_3,
  output Q0_4,
  output Q0_5,
  output Q0_6,
  output Q2_3,
  output Q2_4,
  output Q1_3,
  output Q1_4,
  output Q1_5,
  output Q1_6,
  output Q3_3,
  output Q2_5,
  output Q3_4,
  output Q2_6,
  output Q3_5,
  output Q3_6
);

  wire AND_2_out, AND_3_out, AND_4_out, AND_5_out, AND_6_out, AND_7_out, AND_8_out, AND_9_out, AND_14_out,
       AND_15_out, AND_16_out, AND_17_out, AND_18_out, AND_19_out, and_20_out, and_21_out, and_22_out,
       and_23_out, and_24_out, and_25_out, and_34_out, and_35_out, and_36_out, and_37_out, and_38_out,
       and_39_out, and_40_out, AND_41_out, AND_out, NAND_2_out, NAND_3_out, NAND_4_out, NAND_5_out,
       NAND_6_out, NAND_7_out, NAND_8_out, NAND_9_out, NAND_10_out, NAND_11_out, NAND_12_out, NAND_13_out,
       NAND_14_out, NAND_15_out, nand_16_out, NAND_out, nor_2_out, NOR_out, not_1_out, not_2_out, not_3_out,
       not_4_out, not_5_out, not_6_out, not_7_out, not_8_out, not_9_out, not_10_out, not_11_out, not_12_out,
       not_13_out, not_14_out, not_15_out, not_16_out, not_17_out, not_18_out, not_19_out, not_20_out,
       not_21_out, not_22_out, not_23_out, not_24_out, not_25_out, not_26_out, not_27_out, not_28_out,
       not_29_out, not_30_out, not_31_out, not_32_out, not_33_out, not_34_out, not_35_out, not_36_out,
       not_37_out, OR_2_out, OR_3_out, or_4_out, OR_5_out, OR_6_out, OR_7_out, or_8_out, or_10_out,
       or_11_out, OR_out, xnor_1_out, xnor_2_out, XOR_2_out, XOR_3_out, XOR_4_out, XOR_5_out, xor_6_out,
       xor_7_out, XOR_out;

  LED led_1 (.in(1'b0));
  LED led_2 (.in(1'b1));
  not not_1 (not_1_out, in_8);
  not not_2 (not_2_out, in_9);
  not not_3 (not_3_out, in_15);
  not not_4 (not_4_out, in_16);
  not not_5 (not_5_out, in_25);
  not not_6 (not_6_out, in_26);
  not not_7 (not_7_out, in_31);
  not not_8 (not_8_out, in_32);
  not not_9 (not_9_out, in_38);
  not not_10 (not_10_out, in_37);
  not not_11 (not_11_out, s1);
  and AND (AND_out, A, B);
  or OR (OR_out, not_1_out, not_2_out);
  nand NAND (NAND_out, in_12, in_14);
  or OR_2 (OR_2_out, not_3_out, not_4_out);
  or OR_3 (OR_3_out, in_21, in_23);
  and AND_2 (AND_2_out, not_5_out, not_6_out);
  nor NOR (NOR_out, in_27, in_29);
  and AND_3 (AND_3_out, not_7_out, not_8_out);
  xor XOR (XOR_out, in_33, in_35);
  and AND_4 (AND_4_out, in_37, not_9_out);
  or or_4 (or_4_out, AND_4_out, AND_5_out);
  and AND_5 (AND_5_out, not_10_out, in_38);
  not not_12 (not_12_out, in_39);
  nand NAND_2 (NAND_2_out, in_40, in_40);
  not not_13 (not_13_out, A0_3);
  not not_14 (not_14_out, A1_3);
  LED led_3 (.in(AND_out));
  not not_15 (not_15_out, OR_out);
  LED led_4 (.in(not_15_out));
  LED led_5 (.in(NAND_out));
  LED led_6 (.in(OR_2_out));
  LED led_7 (.in(OR_3_out));
  not not_16 (not_16_out, AND_2_out);
  LED led_8 (.in(not_16_out));
  LED led_9 (.in(NOR_out));
  LED led_10 (.in(AND_3_out));
  LED led_11 (.in(XOR_out));
  LED led_12 (.in(or_4_out));
  LED led_13 (.in(not_12_out));
  LED led_14 (.in(NAND_2_out));
  xor XOR_2 (XOR_2_out, in_41, in_42);
  xor XOR_3 (XOR_3_out, a_3, b_3);
  and AND_6 (AND_6_out, D0, not_11_out, not_17_out);
  not not_17 (not_17_out, s0);
  and AND_7 (AND_7_out, D1, not_11_out, s0);
  and AND_8 (AND_8_out, D2, s1, not_18_out);
  not not_18 (not_18_out, s0);
  and AND_9 (AND_9_out, D3, s1, s0);
  nand NAND_3 (NAND_3_out, F, in_7);
  nand NAND_4 (NAND_4_out, in_28, in_28);
  nand NAND_5 (NAND_5_out, in_30, in_30);
  nand NAND_6 (NAND_6_out, in_34, in_36);
  and AND_10 (Q0_6, not_13_out, Enable_2, not_14_out);
  and AND_11 (Q1_4, A0_3, Enable_2, not_14_out);
  and AND_12 (Q2_6, A1_3, Enable_2, not_13_out);
  and AND_13 (Q3_6, A1_3, Enable_2, A0_3);
  LED led_15 (.in(NAND_7_out));
  nand NAND_7 (NAND_7_out, NAND_3_out, NAND_3_out);
  nand NAND_8 (NAND_8_out, in_22, in_22);
  nand NAND_9 (NAND_9_out, NAND_8_out, NAND_10_out);
  nand NAND_10 (NAND_10_out, in_24, in_24);
  nand NAND_11 (NAND_11_out, NAND_4_out, NAND_5_out);
  nand NAND_12 (NAND_12_out, in_34, NAND_6_out);
  nand NAND_13 (NAND_13_out, NAND_6_out, in_36);
  xor XOR_4 (XOR_4_out, XOR_2_out, Carry_in);
  and AND_14 (AND_14_out, XOR_2_out, Carry_in);
  and AND_15 (AND_15_out, in_41, in_42);
  xor XOR_5 (XOR_5_out, XOR_3_out, Carry_in_2);
  and AND_16 (AND_16_out, b_3, a_3);
  and AND_17 (AND_17_out, b_3, Carry_in_2);
  and AND_18 (AND_18_out, a_3, Carry_in_2);
  or OR_5 (OR_5_out, AND_6_out, AND_7_out, AND_8_out, AND_9_out);
  LED led_16 (.in(OR_5_out));
  Decoder #(.select(2)) decoder_1 (.out0(Q0_3), .out1(Q2_3), .out2(Q1_5), .out3(Q3_3), .sel(A_5), .en(Enable));
  LED led_17 (.in(NAND_9_out));
  LED led_18 (.in(NAND_14_out));
  nand NAND_14 (NAND_14_out, NAND_11_out, NAND_11_out);
  LED led_19 (.in(NAND_15_out));
  nand NAND_15 (NAND_15_out, NAND_12_out, NAND_13_out);
  LED led_20 (.in(XOR_4_out));
  LED led_21 (.in(OR_6_out));
  or OR_6 (OR_6_out, AND_14_out, AND_15_out);
  LED led_22 (.in(XOR_5_out));
  LED led_23 (.in(OR_7_out));
  or OR_7 (OR_7_out, AND_16_out, AND_17_out, AND_18_out);
  not not_19 (not_19_out, A0);
  not not_20 (not_20_out, A1);
  not not_21 (not_21_out, en2a____0_2);
  not not_22 (not_22_out, en2b___0_2);
  not not_23 (not_23_out, A0_2);
  not not_24 (not_24_out, A1_2);
  and AND_19 (AND_19_out, en1___1_2, not_21_out, not_22_out);
  and and_20 (and_20_out, a_2, b_2);
  and and_21 (and_21_out, a_2, c);
  and and_22 (and_22_out, b_2, c);
  and and_23 (and_23_out, a_2, d);
  and and_24 (and_24_out, b_2, d);
  and and_25 (and_25_out, c, d);
  xor odd_parity_1 (s, a_2, b_2, c, d);
  and AND_26 (Q0_2, not_19_out, not_20_out);
  and AND_27 (Q1, A0, not_20_out);
  and AND_28 (Q2_2, A1, not_19_out);
  and AND_29 (Q3_2, A1, A0);
  not not_25 (not_25_out, x);
  not not_26 (not_26_out, y);
  not not_27 (not_27_out, z);
  not not_28 (not_28_out, x_2);
  not not_29 (not_29_out, y_2);
  and AND_30 (Q0_4, not_23_out, AND_19_out, not_24_out);
  and AND_31 (Q1_3, A0_2, AND_19_out, not_24_out);
  and AND_32 (Q2_5, A1_2, AND_19_out, not_23_out);
  and AND_33 (Q3_5, A1_2, AND_19_out, A0_2);
  and and_34 (and_34_out, not_25_out, not_26_out, not_27_out);
  not not_30 (not_30_out, x);
  and and_35 (and_35_out, not_30_out, z, not_31_out);
  not not_31 (not_31_out, y);
  and and_36 (and_36_out, not_28_out, y_2);
  or or_8 (or_8_out, x_2, not_29_out, z_2);
  and and_37 (and_37_out, in_17, in_18);
  not not_32 (not_32_out, in_19);
  and and_38 (and_38_out, in_19, not_33_out);
  not not_33 (not_33_out, in_20);
  or or_9 (cout, and_20_out, and_21_out, and_22_out, and_23_out, and_24_out, and_25_out);
  Decoder #(.select(2), .enable("false")) decoder_2 (.out0(Q0), .out1(Q2), .out2(Q1_2), .out3(Q3), .sel(A_4));
  or or_10 (or_10_out, and_34_out, and_35_out);
  not not_34 (not_34_out, and_36_out);
  not not_35 (not_35_out, or_8_out);
  nor nor_2 (nor_2_out, in_17, in_19, in_20);
  xor xor_6 (xor_6_out, in_19, in_20);
  xnor xnor_1 (xnor_1_out, in_17, in_18);
  not not_36 (not_36_out, en2a____0);
  not not_37 (not_37_out, en2b___0);
  LED led_24 (.in(or_10_out));
  xnor xnor_2 (xnor_2_out, not_34_out, not_35_out);
  and and_39 (and_39_out, and_37_out, or_11_out);
  or or_11 (or_11_out, not_32_out, xor_6_out);
  and and_40 (and_40_out, xnor_1_out, and_38_out);
  and AND_41 (AND_41_out, en1___1, not_36_out, not_37_out);
  LED led_25 (.in(nand_16_out));
  nand nand_16 (nand_16_out, xnor_2_out, z_2);
  Decoder #(.select(2)) decoder_3 (.out0(Q0_5), .out1(Q2_4), .out2(Q1_6), .out3(Q3_4), .sel(A_6), .en(AND_41_out));
  ExactlyOne xor_7 (.out(xor_7_out), .in0(nor_2_out), .in1(and_39_out), .in2(and_40_out));
  LED led_26 (.in(xor_7_out));

  // Notes on the sheet:
  //   Porta Conectivo de Sheffer (NAND)
  //   Não (NOT)
  //   Porta E (AND)
  //   Porta OU (OR)
  //   Porta  (NOR)
  //   Porta XOU (XOR)
  //   NOT
  //   Somador Completo de 3 bits
  //   Multiplexador de 4 entradas
  //   A.B=F
  //   A+B=F
  //   A=F
  //   Decodificador de 2 entradas e 4 saídas com enable
  //   A+B=F
  //   A⊕B=F
  //   input
  //   A
  //   0
  //   0
  //   1
  //   1
  //   A
  //   0
  //   0
  //   1
  //   1
  //   input
  //   A
  //   0
  //   0
  //   1
  //   1
  //   Y
  //   B
  //   0
  //   1
  //   0
  //   1
  //   A.B=F
  //   input
  //   B
  //   0
  //   1
  //   0
  //   1
  //   B
  //   0
  //   1
  //   0
  //   1
  //   input
  //   A
  //   B
  //   0
  //   0
  //   1
  //   0
  //   0
  //   1
  //   1
  //   1
  //   input
  //   A
  //   B
  //   0
  //   0
  //   1
  //   0
  //   0
  //   1
  //   1
  //   1
  //   s
  //   carry out
  //   output
  //   F
  //   0
  //   0
  //   0
  //   1
  //   output
  //   F
  //   1
  //   1
  //   1
  //   0
  //   output
  //   F
  //   0
  //   1
  //   1
  //   1
  //   output
  //   F
  //   1
  //   0
  //   0
  //   0
  //   output
  //   F
  //   0
  //   1
  //   1
  //   0
  //   Enable
  //   Decodificador de 2 entradas e 4 saídas
  //   f3
  //   W
  //   Somador  de 4 bits
  //   Decodificador de 2 entradas e 4 saídas com enable de 3
  //   Enable
endmodule

module aaa (
  input  a,
  input  b,
  input  c,
  input  d,
  output cout,
  output s
);

  wire and_1_out, and_2_out, and_3_out, and_4_out, and_5_out, and_6_out;

  and and_1 (and_1_out, a, b);
  and and_2 (and_2_out, a, c);
  and and_3 (and_3_out, b, c);
  and and_4 (and_4_out, a, d);
  and and_5 (and_5_out, b, d);
  and and_6 (and_6_out, c, d);
  xor odd_parity_1 (s, a, b, c, d);
  or or_1 (cout, and_1_out, and_2_out, and_3_out, and_4_out, and_5_out, and_6_out);
endmodule
